// Logisim project UlaSimples.circ as structural Verilog: 9 circuits, main circuit main
module main (
);


  // Notes on the sheet:
  //   soma naturais, soma inteiros, deslocamento, 
endmodule

module MUX4 (
  input  in_1,
  input  in_2,
  input  in_3,
  input  in_4,
  input  in_5,
  input  in_6,
  output out_7
);

  wire and_1_out, and_2_out, and_3_out, and_4_out;

  and and_1 (and_1_out, in_1, ~in_5, ~in_6);  // AND_Gate
  and and_2 (and_2_out, in_2, ~in_5, in_6);  // AND_Gate
  and and_3 (and_3_out, in_3, in_5, ~in_6);  // AND_Gate
  and and_4 (and_4_out, in_4, in_5, in_6);
  or or_1 (out_7, and_1_out, and_2_out, and_3_out, and_4_out);
endmodule

module CelulaUla (
  input  A,
  input  B,
  input  sel1,
  input  sel0,
  input  vem1,
  output out_6,
  output vai1
);

  wire adder_1_out, and_1_out, or_1_out, xor_1_out;

  and and_1 (and_1_out, A, B);
  or or_1 (or_1_out, A, B);
  Adder #(.width(1)) adder_1 (.a(A), .b(B), .out(adder_1_out), .cin(vem1), .cout(vai1));
  xor xor_1 (xor_1_out, A, B);
  MUX4 mux4_1 (
    .in_1(and_1_out), .in_2(or_1_out), .in_3(xor_1_out), .in_4(adder_1_out), .in_5(sel1), .in_6(sel0),
    .out_7(out_6));

  // Notes on the sheet:
  //   tem que ter 32 bits nossa ula
  //   Tem que fazer o proprio somador
  //   Ta errado
endmodule

module ShigLEftLogival1bit (
  input  [3:0] in_1,
  output [3:0] out_2
);


  assign out_2 = {in_1[2:0], 1'b0};
endmodule

module ShiftRightLogical1bit (
  input  [3:0] in_1,
  output [3:0] out_2
);


  assign out_2 = {1'b0, in_1[3:1]};
endmodule

module ShiftRightArith1bit (
  input  [3:0] in_1,
  output [3:0] out_2
);


  assign out_2 = {{2{in_1[3]}}, in_1[2:1]};
endmodule

module SLLDetect (
  input  [2:0] ALUOpCode,
  output sll
);

  and and_1 (sll, ~ALUOpCode[0], ~ALUOpCode[1], ALUOpCode[2]);  // AND_Gate
endmodule

module SLDDetect (
  input  [2:0] ALUOpCode,
  output sld
);

  and and_1 (sld, ALUOpCode[0], ~ALUOpCode[1], ALUOpCode[2]);  // AND_Gate
endmodule

module SRADetect (
  input  [2:0] ALUOpCode,
  output slr
);

  and and_1 (slr, ALUOpCode[0], ALUOpCode[1], ALUOpCode[2]);
endmodule
