// Logisim project aulaBancoRegistrador.circ as structural Verilog: 5 circuits, main circuit main
module main (
  input  in_1,
  input  [3:0] in_2,
  input  [3:0] in_3,
  input  [2:0] in_4
);

  wire [3:0] undriven, undriven_2;

  Banco8Reg4Bits banco8reg4bits_1 (
    .ViewRegA(undriven), .View(undriven_2));  // open: Reset, in_4, in_1, OpCode, in_8, in_5
  ULA ula_1 (.A(undriven), .B(undriven_2), .OpCode(in_1));  // open: S

  // Notes on the sheet:
  //   Me perdi
endmodule

module Registrador4Bits (
  input  [3:0] in_1,
  input  Save,
  input  Reset,
  output [3:0] out_4
);

  wire [3:0] d_ff_4_q;

  D_Flip_Flop d_ff_1 (.clk(Save), .D(in_1[3]), .Q(d_ff_4_q[3]), .reset(Reset));  // open: Qn, preset, en
  D_Flip_Flop d_ff_2 (.clk(Save), .D(in_1[2]), .Q(d_ff_4_q[2]), .reset(Reset));  // open: Qn, preset, en
  D_Flip_Flop d_ff_3 (.clk(Save), .D(in_1[1]), .Q(d_ff_4_q[1]), .reset(Reset));  // open: Qn, preset, en
  D_Flip_Flop d_ff_4 (.clk(Save), .D(in_1[0]), .Q(d_ff_4_q[0]), .reset(Reset));  // open: Qn, preset, en

  // Notes on the sheet:
  //   quando clock da 1, se D tiver 0 ele nao sai 1. quando D ta 1 se clock virar 1 a saida é 1
endmodule

module Banco8Reg4Bits (
  input  [3:0] in_1,
  input  Reset,
  input  [3:0] ViewRegA,
  input  in_4,
  input  [2:0] in_5,
  input  [2:0] OpCode,
  input  [3:0] View,
  input  [2:0] in_8
);

  wire demultiplexer_1_out0, demultiplexer_1_out1, demultiplexer_1_out2, demultiplexer_1_out3,
       demultiplexer_1_out4, demultiplexer_1_out5, demultiplexer_1_out6, demultiplexer_1_out7;
  wire [3:0] undriven, undriven_2, undriven_3, undriven_4, undriven_5, undriven_6, undriven_7, undriven_8;

  Demultiplexer #(.select(3), .enable("false")) demultiplexer_1 (
    .out0(demultiplexer_1_out0), .out1(demultiplexer_1_out1), .out2(demultiplexer_1_out2),
    .out3(demultiplexer_1_out3), .out4(demultiplexer_1_out4), .out5(demultiplexer_1_out5),
    .out6(demultiplexer_1_out6), .out7(demultiplexer_1_out7), .in(in_4), .sel(OpCode));
  Registrador4Bits registrador4bits_1 (.Save(demultiplexer_1_out0), .Reset(Reset), .in_1(undriven), .out_4(in_1));
  Registrador4Bits registrador4bits_2 (.Save(demultiplexer_1_out1), .in_1(undriven_2), .out_4(in_1));  // open: Reset
  Registrador4Bits registrador4bits_3 (.Save(demultiplexer_1_out2), .Reset(Reset), .in_1(undriven_3), .out_4(in_1));
  Registrador4Bits registrador4bits_4 (.Save(demultiplexer_1_out3), .Reset(Reset), .in_1(undriven_6), .out_4(in_1));
  Registrador4Bits registrador4bits_5 (.Save(demultiplexer_1_out4), .Reset(Reset), .in_1(undriven_4), .out_4(in_1));
  Registrador4Bits registrador4bits_6 (.Save(demultiplexer_1_out5), .Reset(Reset), .in_1(undriven_7), .out_4(in_1));
  Registrador4Bits registrador4bits_7 (.Save(demultiplexer_1_out6), .Reset(Reset), .in_1(undriven_8), .out_4(in_1));
  Registrador4Bits registrador4bits_8 (.Save(demultiplexer_1_out7), .Reset(Reset), .in_1(undriven_5), .out_4(in_1));
  Multiplexer #(.select(3), .width(4), .enable("false")) multiplexer_1 (
    .in0(undriven), .in1(undriven_2), .in2(undriven_3), .in3(undriven_6), .in4(undriven_4), .in5(undriven_7),
    .in6(undriven_8), .in7(undriven_5), .out(View), .sel(in_8));
  Multiplexer #(.select(3), .width(4), .enable("false")) multiplexer_2 (
    .in0(undriven), .in1(undriven_2), .in2(undriven_3), .in3(undriven_6), .in4(undriven_4), .in5(undriven_7),
    .in6(undriven_8), .in7(undriven_5), .out(ViewRegA), .sel(in_5));
endmodule

module ULA (
  input  [3:0] A,
  input  [3:0] B,
  input  OpCode,
  output [3:0] S
);

  wire [3:0] adder_1_out, and_1_out;

  assign and_1_out = A & B;  // AND_Gate and_1, 4 bits wide
  Adder #(.width(4)) adder_1 (.a(A), .b(B), .out(adder_1_out), .cin(1'b0));  // open: cout
  Multiplexer #(.width(4), .enable("false")) multiplexer_1 (.in0(and_1_out), .in1(adder_1_out), .out(S), .sel(OpCode));
endmodule

module Reg4Original (
  input  in_1,
  input  in_2,
  input  in_3,
  input  in_4,
  input  clock,
  input  Reset,
  output out_7,
  output out_8,
  output out_9,
  output out_10
);

  wire undriven;

  D_Flip_Flop d_ff_1 (.clk(clock), .D(in_1), .Q(out_7), .reset(Reset));  // open: Qn, preset, en
  D_Flip_Flop d_ff_2 (.clk(clock), .D(in_2), .Q(out_8), .reset(Reset));  // open: Qn, preset, en
  D_Flip_Flop d_ff_3 (.clk(undriven), .D(in_3), .Q(out_9), .reset(Reset));  // open: Qn, preset, en
  D_Flip_Flop d_ff_4 (.clk(undriven), .D(in_4), .Q(out_10), .reset(Reset));  // open: Qn, preset, en

  // Notes on the sheet:
  //   quando clock da 1, se D tiver 0 ele nao sai 1. quando D ta 1 se clock virar 1 a saida é 1
endmodule
