// Logisim project bancoRegistrador.circ as structural Verilog: 4 circuits, main circuit main
module main (
  input  [31:0] DataIn,
  input  DataIn_2,
  input  Reset,
  input  [31:0] DataOut
);

  D_Flip_Flop d_ff_1 (.clk(DataIn_2), .D(DataIn[31]), .Q(DataOut[31]), .reset(Reset));  // open: Qn, preset, en
  D_Flip_Flop d_ff_2 (.clk(DataIn_2), .D(DataIn[30]), .Q(DataOut[30]), .reset(Reset));  // open: Qn, preset, en
  D_Flip_Flop d_ff_3 (.clk(DataIn_2), .D(DataIn[29]), .Q(DataOut[29]), .reset(Reset));  // open: Qn, preset, en
  D_Flip_Flop d_ff_4 (.clk(DataIn_2), .D(DataIn[28]), .Q(DataOut[28]), .reset(Reset));  // open: Qn, preset, en
  D_Flip_Flop d_ff_5 (.clk(DataIn_2), .D(DataIn[27]), .Q(DataOut[27]), .reset(Reset));  // open: Qn, preset, en
  D_Flip_Flop d_ff_6 (.clk(DataIn_2), .D(DataIn[26]), .Q(DataOut[26]), .reset(Reset));  // open: Qn, preset, en
  D_Flip_Flop d_ff_7 (.clk(DataIn_2), .D(DataIn[25]), .Q(DataOut[25]), .reset(Reset));  // open: Qn, preset, en
  D_Flip_Flop d_ff_8 (.clk(DataIn_2), .D(DataIn[24]), .Q(DataOut[24]), .reset(Reset));  // open: Qn, preset, en
  D_Flip_Flop d_ff_9 (.clk(DataIn_2), .D(DataIn[23]), .Q(DataOut[23]), .reset(Reset));  // open: Qn, preset, en
  D_Flip_Flop d_ff_10 (.clk(DataIn_2), .D(DataIn[22]), .Q(DataOut[22]), .reset(Reset));  // open: Qn, preset, en
  D_Flip_Flop d_ff_11 (.clk(DataIn_2), .D(DataIn[21]), .Q(DataOut[21]), .reset(Reset));  // open: Qn, preset, en
  D_Flip_Flop d_ff_12 (.clk(DataIn_2), .D(DataIn[20]), .Q(DataOut[20]), .reset(Reset));  // open: Qn, preset, en
  D_Flip_Flop d_ff_13 (.clk(DataIn_2), .D(DataIn[19]), .Q(DataOut[19]), .reset(Reset));  // open: Qn, preset, en
  D_Flip_Flop d_ff_14 (.clk(DataIn_2), .D(DataIn[18]), .Q(DataOut[18]), .reset(Reset));  // open: Qn, preset, en
  D_Flip_Flop d_ff_15 (.clk(DataIn_2), .D(DataIn[17]), .Q(DataOut[17]), .reset(Reset));  // open: Qn, preset, en
  D_Flip_Flop d_ff_16 (.clk(DataIn_2), .D(DataIn[16]), .Q(DataOut[16]), .reset(Reset));  // open: Qn, preset, en
  D_Flip_Flop d_ff_17 (.clk(DataIn_2), .D(DataIn[15]), .Q(DataOut[15]), .reset(Reset));  // open: Qn, preset, en
  D_Flip_Flop d_ff_18 (.clk(DataIn_2), .D(DataIn[14]), .Q(DataOut[14]), .reset(Reset));  // open: Qn, preset, en
  D_Flip_Flop d_ff_19 (.clk(DataIn_2), .D(DataIn[13]), .Q(DataOut[13]), .reset(Reset));  // open: Qn, preset, en
  D_Flip_Flop d_ff_20 (.clk(DataIn_2), .D(DataIn[12]), .Q(DataOut[12]), .reset(Reset));  // open: Qn, preset, en
  D_Flip_Flop d_ff_21 (.clk(DataIn_2), .D(DataIn[11]), .Q(DataOut[11]), .reset(Reset));  // open: Qn, preset, en
  D_Flip_Flop d_ff_22 (.clk(DataIn_2), .D(DataIn[10]), .Q(DataOut[10]), .reset(Reset));  // open: Qn, preset, en
  D_Flip_Flop d_ff_23 (.clk(DataIn_2), .D(DataIn[9]), .Q(DataOut[9]), .reset(Reset));  // open: Qn, preset, en
  D_Flip_Flop d_ff_24 (.clk(DataIn_2), .D(DataIn[8]), .Q(DataOut[8]), .reset(Reset));  // open: Qn, preset, en
  D_Flip_Flop d_ff_25 (.clk(DataIn_2), .D(DataIn[7]), .Q(DataOut[7]), .reset(Reset));  // open: Qn, preset, en
  D_Flip_Flop d_ff_26 (.clk(DataIn_2), .D(DataIn[6]), .Q(DataOut[6]), .reset(Reset));  // open: Qn, preset, en
  D_Flip_Flop d_ff_27 (.clk(DataIn_2), .D(DataIn[5]), .Q(DataOut[5]), .reset(Reset));  // open: Qn, preset, en
  D_Flip_Flop d_ff_28 (.clk(DataIn_2), .D(DataIn[4]), .Q(DataOut[4]), .reset(Reset));  // open: Qn, preset, en
  D_Flip_Flop d_ff_29 (.clk(DataIn_2), .D(DataIn[3]), .Q(DataOut[3]), .reset(Reset));  // open: Qn, preset, en
  D_Flip_Flop d_ff_30 (.clk(DataIn_2), .D(DataIn[2]), .Q(DataOut[2]), .reset(Reset));  // open: Qn, preset, en
  D_Flip_Flop d_ff_31 (.clk(DataIn_2), .D(DataIn[1]), .Q(DataOut[1]), .reset(Reset));  // open: Qn, preset, en
  D_Flip_Flop d_ff_32 (.clk(DataIn_2), .D(DataIn[0]), .Q(DataOut[0]), .reset(Reset));  // open: Qn, preset, en
endmodule

module Registrador32bit (
  input  [31:0] DataIn,
  input  Save,
  input  Reset,
  output [31:0] DataOut
);

  D_Flip_Flop d_ff_1 (.clk(Save), .D(DataIn[31]), .Q(DataOut[31]), .reset(Reset));  // open: Qn, preset, en
  D_Flip_Flop d_ff_2 (.clk(Save), .D(DataIn[30]), .Q(DataOut[30]), .reset(Reset));  // open: Qn, preset, en
  D_Flip_Flop d_ff_3 (.clk(Save), .D(DataIn[29]), .Q(DataOut[29]), .reset(Reset));  // open: Qn, preset, en
  D_Flip_Flop d_ff_4 (.clk(Save), .D(DataIn[28]), .Q(DataOut[28]), .reset(Reset));  // open: Qn, preset, en
  D_Flip_Flop d_ff_5 (.clk(Save), .D(DataIn[27]), .Q(DataOut[27]), .reset(Reset));  // open: Qn, preset, en
  D_Flip_Flop d_ff_6 (.clk(Save), .D(DataIn[26]), .Q(DataOut[26]), .reset(Reset));  // open: Qn, preset, en
  D_Flip_Flop d_ff_7 (.clk(Save), .D(DataIn[25]), .Q(DataOut[25]), .reset(Reset));  // open: Qn, preset, en
  D_Flip_Flop d_ff_8 (.clk(Save), .D(DataIn[24]), .Q(DataOut[24]), .reset(Reset));  // open: Qn, preset, en
  D_Flip_Flop d_ff_9 (.clk(Save), .D(DataIn[23]), .Q(DataOut[23]), .reset(Reset));  // open: Qn, preset, en
  D_Flip_Flop d_ff_10 (.clk(Save), .D(DataIn[22]), .Q(DataOut[22]), .reset(Reset));  // open: Qn, preset, en
  D_Flip_Flop d_ff_11 (.clk(Save), .D(DataIn[21]), .Q(DataOut[21]), .reset(Reset));  // open: Qn, preset, en
  D_Flip_Flop d_ff_12 (.clk(Save), .D(DataIn[20]), .Q(DataOut[20]), .reset(Reset));  // open: Qn, preset, en
  D_Flip_Flop d_ff_13 (.clk(Save), .D(DataIn[19]), .Q(DataOut[19]), .reset(Reset));  // open: Qn, preset, en
  D_Flip_Flop d_ff_14 (.clk(Save), .D(DataIn[18]), .Q(DataOut[18]), .reset(Reset));  // open: Qn, preset, en
  D_Flip_Flop d_ff_15 (.clk(Save), .D(DataIn[17]), .Q(DataOut[17]), .reset(Reset));  // open: Qn, preset, en
  D_Flip_Flop d_ff_16 (.clk(Save), .D(DataIn[16]), .Q(DataOut[16]), .reset(Reset));  // open: Qn, preset, en
  D_Flip_Flop d_ff_17 (.clk(Save), .D(DataIn[15]), .Q(DataOut[15]), .reset(Reset));  // open: Qn, preset, en
  D_Flip_Flop d_ff_18 (.clk(Save), .D(DataIn[14]), .Q(DataOut[14]), .reset(Reset));  // open: Qn, preset, en
  D_Flip_Flop d_ff_19 (.clk(Save), .D(DataIn[13]), .Q(DataOut[13]), .reset(Reset));  // open: Qn, preset, en
  D_Flip_Flop d_ff_20 (.clk(Save), .D(DataIn[12]), .Q(DataOut[12]), .reset(Reset));  // open: Qn, preset, en
  D_Flip_Flop d_ff_21 (.clk(Save), .D(DataIn[11]), .Q(DataOut[11]), .reset(Reset));  // open: Qn, preset, en
  D_Flip_Flop d_ff_22 (.clk(Save), .D(DataIn[10]), .Q(DataOut[10]), .reset(Reset));  // open: Qn, preset, en
  D_Flip_Flop d_ff_23 (.clk(Save), .D(DataIn[9]), .Q(DataOut[9]), .reset(Reset));  // open: Qn, preset, en
  D_Flip_Flop d_ff_24 (.clk(Save), .D(DataIn[8]), .Q(DataOut[8]), .reset(Reset));  // open: Qn, preset, en
  D_Flip_Flop d_ff_25 (.clk(Save), .D(DataIn[7]), .Q(DataOut[7]), .reset(Reset));  // open: Qn, preset, en
  D_Flip_Flop d_ff_26 (.clk(Save), .D(DataIn[6]), .Q(DataOut[6]), .reset(Reset));  // open: Qn, preset, en
  D_Flip_Flop d_ff_27 (.clk(Save), .D(DataIn[5]), .Q(DataOut[5]), .reset(Reset));  // open: Qn, preset, en
  D_Flip_Flop d_ff_28 (.clk(Save), .D(DataIn[4]), .Q(DataOut[4]), .reset(Reset));  // open: Qn, preset, en
  D_Flip_Flop d_ff_29 (.clk(Save), .D(DataIn[3]), .Q(DataOut[3]), .reset(Reset));  // open: Qn, preset, en
  D_Flip_Flop d_ff_30 (.clk(Save), .D(DataIn[2]), .Q(DataOut[2]), .reset(Reset));  // open: Qn, preset, en
  D_Flip_Flop d_ff_31 (.clk(Save), .D(DataIn[1]), .Q(DataOut[1]), .reset(Reset));  // open: Qn, preset, en
  D_Flip_Flop d_ff_32 (.clk(Save), .D(DataIn[0]), .Q(DataOut[0]), .reset(Reset));  // open: Qn, preset, en
endmodule

module Banco32Reg32 (
  input  [31:0] Data,
  input  Reset,
  input  CLK,
  input  [4:0] RegW,
  input  [4:0] RegA,
  input  [4:0] RegB,
  output [31:0] ViewRegA,
  output [31:0] ViewRegB
);

  wire demultiplexer_1_out0, demultiplexer_1_out1, demultiplexer_1_out2, demultiplexer_1_out3,
       demultiplexer_1_out4, demultiplexer_1_out5, demultiplexer_1_out6, demultiplexer_1_out7,
       demultiplexer_1_out8, demultiplexer_1_out9, demultiplexer_1_out10, demultiplexer_1_out11,
       demultiplexer_1_out12, demultiplexer_1_out13, demultiplexer_1_out14, demultiplexer_1_out15,
       demultiplexer_1_out16, demultiplexer_1_out17, demultiplexer_1_out18, demultiplexer_1_out19,
       demultiplexer_1_out20, demultiplexer_1_out21, demultiplexer_1_out22, demultiplexer_1_out23,
       demultiplexer_1_out24, demultiplexer_1_out25, demultiplexer_1_out26, demultiplexer_1_out27,
       demultiplexer_1_out28, demultiplexer_1_out29, demultiplexer_1_out30, demultiplexer_1_out31;
  wire [31:0] registrador32bit_1_dataout, registrador32bit_2_dataout, registrador32bit_3_dataout,
       registrador32bit_4_dataout, registrador32bit_5_dataout, registrador32bit_6_dataout,
       registrador32bit_7_dataout, registrador32bit_8_dataout, registrador32bit_9_dataout,
       registrador32bit_10_dataout, registrador32bit_11_dataout, registrador32bit_12_dataout,
       registrador32bit_13_dataout, registrador32bit_14_dataout, registrador32bit_15_dataout,
       registrador32bit_16_dataout, registrador32bit_17_dataout, registrador32bit_18_dataout,
       registrador32bit_19_dataout, registrador32bit_20_dataout, registrador32bit_21_dataout,
       registrador32bit_22_dataout, registrador32bit_23_dataout, registrador32bit_24_dataout,
       registrador32bit_25_dataout, registrador32bit_26_dataout, registrador32bit_27_dataout,
       registrador32bit_28_dataout, registrador32bit_29_dataout, registrador32bit_30_dataout,
       registrador32bit_31_dataout, registrador32bit_32_dataout;

  Demultiplexer #(.select(5), .enable("false")) demultiplexer_1 (
    .out0(demultiplexer_1_out0), .out1(demultiplexer_1_out1), .out2(demultiplexer_1_out2),
    .out3(demultiplexer_1_out3), .out4(demultiplexer_1_out4), .out5(demultiplexer_1_out5),
    .out6(demultiplexer_1_out6), .out7(demultiplexer_1_out7), .out8(demultiplexer_1_out8),
    .out9(demultiplexer_1_out9), .out10(demultiplexer_1_out10), .out11(demultiplexer_1_out11),
    .out12(demultiplexer_1_out12), .out13(demultiplexer_1_out13), .out14(demultiplexer_1_out14),
    .out15(demultiplexer_1_out15), .out16(demultiplexer_1_out16), .out17(demultiplexer_1_out17),
    .out18(demultiplexer_1_out18), .out19(demultiplexer_1_out19), .out20(demultiplexer_1_out20),
    .out21(demultiplexer_1_out21), .out22(demultiplexer_1_out22), .out23(demultiplexer_1_out23),
    .out24(demultiplexer_1_out24), .out25(demultiplexer_1_out25), .out26(demultiplexer_1_out26),
    .out27(demultiplexer_1_out27), .out28(demultiplexer_1_out28), .out29(demultiplexer_1_out29),
    .out30(demultiplexer_1_out30), .out31(demultiplexer_1_out31), .in(CLK), .sel(RegW));
  Registrador32bit registrador32bit_1 (
    .DataIn(Data), .Save(demultiplexer_1_out0), .Reset(Reset), .DataOut(registrador32bit_1_dataout));
  Registrador32bit registrador32bit_2 (
    .DataIn(Data), .Save(demultiplexer_1_out1), .Reset(Reset), .DataOut(registrador32bit_2_dataout));
  Registrador32bit registrador32bit_3 (
    .DataIn(Data), .Save(demultiplexer_1_out2), .Reset(Reset), .DataOut(registrador32bit_3_dataout));
  Registrador32bit registrador32bit_4 (
    .DataIn(Data), .Save(demultiplexer_1_out3), .Reset(Reset), .DataOut(registrador32bit_4_dataout));
  Registrador32bit registrador32bit_5 (
    .DataIn(Data), .Save(demultiplexer_1_out4), .Reset(Reset), .DataOut(registrador32bit_5_dataout));
  Registrador32bit registrador32bit_6 (
    .DataIn(Data), .Save(demultiplexer_1_out5), .Reset(Reset), .DataOut(registrador32bit_6_dataout));
  Registrador32bit registrador32bit_7 (
    .DataIn(Data), .Save(demultiplexer_1_out6), .Reset(Reset), .DataOut(registrador32bit_7_dataout));
  Registrador32bit registrador32bit_8 (
    .DataIn(Data), .Save(demultiplexer_1_out7), .Reset(Reset), .DataOut(registrador32bit_8_dataout));
  Registrador32bit registrador32bit_9 (
    .DataIn(Data), .Save(demultiplexer_1_out8), .Reset(Reset), .DataOut(registrador32bit_9_dataout));
  Registrador32bit registrador32bit_10 (
    .DataIn(Data), .Save(demultiplexer_1_out9), .Reset(Reset), .DataOut(registrador32bit_10_dataout));
  Registrador32bit registrador32bit_11 (
    .DataIn(Data), .Save(demultiplexer_1_out10), .Reset(Reset), .DataOut(registrador32bit_11_dataout));
  Registrador32bit registrador32bit_12 (
    .DataIn(Data), .Save(demultiplexer_1_out11), .Reset(Reset), .DataOut(registrador32bit_12_dataout));
  Registrador32bit registrador32bit_13 (
    .DataIn(Data), .Save(demultiplexer_1_out12), .Reset(Reset), .DataOut(registrador32bit_13_dataout));
  Registrador32bit registrador32bit_14 (
    .DataIn(Data), .Save(demultiplexer_1_out13), .Reset(Reset), .DataOut(registrador32bit_14_dataout));
  Registrador32bit registrador32bit_15 (
    .DataIn(Data), .Save(demultiplexer_1_out14), .Reset(Reset), .DataOut(registrador32bit_15_dataout));
  Registrador32bit registrador32bit_16 (
    .DataIn(Data), .Save(demultiplexer_1_out15), .Reset(Reset), .DataOut(registrador32bit_16_dataout));
  Registrador32bit registrador32bit_17 (
    .DataIn(Data), .Save(demultiplexer_1_out16), .Reset(Reset), .DataOut(registrador32bit_17_dataout));
  Registrador32bit registrador32bit_18 (
    .DataIn(Data), .Save(demultiplexer_1_out17), .Reset(Reset), .DataOut(registrador32bit_18_dataout));
  Registrador32bit registrador32bit_19 (
    .DataIn(Data), .Save(demultiplexer_1_out18), .Reset(Reset), .DataOut(registrador32bit_19_dataout));
  Registrador32bit registrador32bit_20 (
    .DataIn(Data), .Save(demultiplexer_1_out19), .Reset(Reset), .DataOut(registrador32bit_20_dataout));
  Registrador32bit registrador32bit_21 (
    .DataIn(Data), .Save(demultiplexer_1_out20), .Reset(Reset), .DataOut(registrador32bit_21_dataout));
  Registrador32bit registrador32bit_22 (
    .DataIn(Data), .Save(demultiplexer_1_out21), .Reset(Reset), .DataOut(registrador32bit_22_dataout));
  Registrador32bit registrador32bit_23 (
    .DataIn(Data), .Save(demultiplexer_1_out22), .Reset(Reset), .DataOut(registrador32bit_23_dataout));
  Registrador32bit registrador32bit_24 (
    .DataIn(Data), .Save(demultiplexer_1_out23), .Reset(Reset), .DataOut(registrador32bit_24_dataout));
  Registrador32bit registrador32bit_25 (
    .DataIn(Data), .Save(demultiplexer_1_out24), .Reset(Reset), .DataOut(registrador32bit_25_dataout));
  Registrador32bit registrador32bit_26 (
    .DataIn(Data), .Save(demultiplexer_1_out25), .Reset(Reset), .DataOut(registrador32bit_26_dataout));
  Registrador32bit registrador32bit_27 (
    .DataIn(Data), .Save(demultiplexer_1_out26), .Reset(Reset), .DataOut(registrador32bit_27_dataout));
  Registrador32bit registrador32bit_28 (
    .DataIn(Data), .Save(demultiplexer_1_out27), .Reset(Reset), .DataOut(registrador32bit_28_dataout));
  Registrador32bit registrador32bit_29 (
    .DataIn(Data), .Save(demultiplexer_1_out28), .Reset(Reset), .DataOut(registrador32bit_29_dataout));
  Registrador32bit registrador32bit_30 (
    .DataIn(Data), .Save(demultiplexer_1_out29), .Reset(Reset), .DataOut(registrador32bit_30_dataout));
  Registrador32bit registrador32bit_31 (
    .DataIn(Data), .Save(demultiplexer_1_out30), .Reset(Reset), .DataOut(registrador32bit_31_dataout));
  Registrador32bit registrador32bit_32 (
    .DataIn(Data), .Save(demultiplexer_1_out31), .Reset(Reset), .DataOut(registrador32bit_32_dataout));
  Multiplexer #(.select(5), .width(32), .enable("false")) multiplexer_1 (
    .in0(registrador32bit_1_dataout), .in1(registrador32bit_2_dataout), .in2(registrador32bit_3_dataout),
    .in3(registrador32bit_4_dataout), .in4(registrador32bit_5_dataout), .in5(registrador32bit_6_dataout),
    .in6(registrador32bit_7_dataout), .in7(registrador32bit_8_dataout), .in8(registrador32bit_9_dataout),
    .in9(registrador32bit_10_dataout), .in10(registrador32bit_11_dataout),
    .in11(registrador32bit_12_dataout), .in12(registrador32bit_13_dataout),
    .in13(registrador32bit_14_dataout), .in14(registrador32bit_15_dataout),
    .in15(registrador32bit_16_dataout), .in16(registrador32bit_17_dataout),
    .in17(registrador32bit_18_dataout), .in18(registrador32bit_19_dataout),
    .in19(registrador32bit_20_dataout), .in20(registrador32bit_21_dataout),
    .in21(registrador32bit_22_dataout), .in22(registrador32bit_23_dataout),
    .in23(registrador32bit_24_dataout), .in24(registrador32bit_25_dataout),
    .in25(registrador32bit_26_dataout), .in26(registrador32bit_27_dataout),
    .in27(registrador32bit_28_dataout), .in28(registrador32bit_29_dataout),
    .in29(registrador32bit_30_dataout), .in30(registrador32bit_31_dataout),
    .in31(registrador32bit_32_dataout), .out(ViewRegA), .sel(RegA));
  Multiplexer #(.select(5), .width(32), .enable("false")) multiplexer_2 (
    .in0(registrador32bit_1_dataout), .in1(registrador32bit_2_dataout), .in2(registrador32bit_3_dataout),
    .in3(registrador32bit_4_dataout), .in4(registrador32bit_5_dataout), .in5(registrador32bit_6_dataout),
    .in6(registrador32bit_7_dataout), .in7(registrador32bit_8_dataout), .in8(registrador32bit_9_dataout),
    .in9(registrador32bit_10_dataout), .in10(registrador32bit_11_dataout),
    .in11(registrador32bit_12_dataout), .in12(registrador32bit_13_dataout),
    .in13(registrador32bit_14_dataout), .in14(registrador32bit_15_dataout),
    .in15(registrador32bit_16_dataout), .in16(registrador32bit_17_dataout),
    .in17(registrador32bit_18_dataout), .in18(registrador32bit_19_dataout),
    .in19(registrador32bit_20_dataout), .in20(registrador32bit_21_dataout),
    .in21(registrador32bit_22_dataout), .in22(registrador32bit_23_dataout),
    .in23(registrador32bit_24_dataout), .in24(registrador32bit_25_dataout),
    .in25(registrador32bit_26_dataout), .in26(registrador32bit_27_dataout),
    .in27(registrador32bit_28_dataout), .in28(registrador32bit_29_dataout),
    .in29(registrador32bit_30_dataout), .in30(registrador32bit_31_dataout),
    .in31(registrador32bit_32_dataout), .out(ViewRegB), .sel(RegB));
endmodule

module Avaliacao (
  input  [31:0] Data,
  input  CLK,
  input  Reset,
  input  [4:0] RegW,
  input  [4:0] RegA,
  input  [4:0] RegB,
  input  Contexto,
  output [31:0] A,
  output [31:0] B
);

  wire demultiplexer_1_out0, demultiplexer_1_out1;
  wire [31:0] banco32reg32_1_viewrega, banco32reg32_1_viewregb, banco32reg32_2_viewrega,
       banco32reg32_2_viewregb;

  Demultiplexer #(.enable("false")) demultiplexer_1 (
    .out0(demultiplexer_1_out0), .out1(demultiplexer_1_out1), .in(CLK), .sel(Contexto));
  Banco32Reg32 banco32reg32_1 (
    .Reset(Reset), .CLK(demultiplexer_1_out0), .Data(Data), .RegW(RegW), .RegA(RegA), .RegB(RegB),
    .ViewRegA(banco32reg32_1_viewrega), .ViewRegB(banco32reg32_1_viewregb));
  Banco32Reg32 banco32reg32_2 (
    .Reset(Reset), .CLK(demultiplexer_1_out1), .Data(Data), .RegW(RegW), .RegA(RegA), .RegB(RegB),
    .ViewRegA(banco32reg32_2_viewrega), .ViewRegB(banco32reg32_2_viewregb));
  Multiplexer #(.width(32), .enable("false")) multiplexer_1 (
    .in0(banco32reg32_1_viewrega), .in1(banco32reg32_2_viewrega), .out(A), .sel(Contexto));
  Multiplexer #(.width(32), .enable("false")) multiplexer_2 (
    .in0(banco32reg32_1_viewregb), .in1(banco32reg32_2_viewregb), .out(B), .sel(Contexto));
endmodule
