// Logisim project mux32.circ as structural Verilog: 1 circuit, main circuit main
module main (
  input  e0,
  input  e1,
  input  e2,
  input  e3,
  input  e4,
  input  e5,
  input  e6,
  input  e7,
  input  e8,
  input  e9,
  input  e10,
  input  e11,
  input  e12,
  input  e13,
  input  e14,
  input  e15,
  input  e16,
  input  e17,
  input  e18,
  input  e19,
  input  e20,
  input  e21,
  input  e22,
  input  e23,
  input  e24,
  input  e25,
  input  e26,
  input  e27,
  input  e28,
  input  e29,
  input  e30,
  input  e31,
  input  sel4,
  input  se3,
  input  sel2,
  input  sel1,
  input  sel0,
  output Saida
);

  wire and_1_out, and_2_out, and_3_out, and_4_out, and_5_out, and_6_out, and_7_out, and_8_out, and_9_out,
       and_10_out, and_11_out, and_12_out, and_13_out, and_14_out, and_15_out, and_16_out, and_17_out,
       and_18_out, and_19_out, and_20_out, and_21_out, and_22_out, and_23_out, and_24_out, and_25_out,
       and_26_out, and_27_out, and_28_out, and_29_out, and_30_out, and_31_out, and_32_out;

  and and_1 (and_1_out, e0, ~sel4, ~se3, ~sel2, ~sel1, ~sel0);  // AND_Gate
  and and_2 (and_2_out, e1, ~sel4, ~se3, ~sel2, ~sel1, sel0);  // AND_Gate
  and and_3 (and_3_out, e2, ~sel4, ~se3, ~sel2, sel1, ~sel0);  // AND_Gate
  and and_4 (and_4_out, e3, ~sel4, ~se3, ~sel2, sel1, sel0);  // AND_Gate
  and and_5 (and_5_out, e4, ~sel4, ~se3, sel2, ~sel1, ~sel0);  // AND_Gate
  and and_6 (and_6_out, e5, ~sel4, ~se3, sel2, ~sel1, sel0);  // AND_Gate
  and and_7 (and_7_out, e6, ~sel4, ~se3, sel2, sel1, ~sel0);  // AND_Gate
  and and_8 (and_8_out, e7, ~sel4, ~se3, sel2, sel1, sel0);  // AND_Gate
  and and_9 (and_9_out, e8, ~sel4, se3, ~sel2, ~sel1, ~sel0);  // AND_Gate
  and and_10 (and_10_out, e9, ~sel4, se3, ~sel2, ~sel1, sel0);  // AND_Gate
  and and_11 (and_11_out, e10, ~sel4, se3, ~sel2, sel1, ~sel0);  // AND_Gate
  and and_12 (and_12_out, e11, ~sel4, se3, ~sel2, sel1, sel0);  // AND_Gate
  and and_13 (and_13_out, e12, ~sel4, se3, sel2, ~sel1, ~sel0);  // AND_Gate
  and and_14 (and_14_out, e13, ~sel4, se3, sel2, ~sel1, sel0);  // AND_Gate
  and and_15 (and_15_out, e14, ~sel4, se3, sel2, sel1, ~sel0);  // AND_Gate
  and and_16 (and_16_out, e15, ~sel4, se3, sel2, sel1, sel0);  // AND_Gate
  and and_17 (and_17_out, e16, sel4, ~se3, ~sel2, ~sel1, ~sel0);  // AND_Gate
  and and_18 (and_18_out, e17, sel4, ~se3, ~sel2, ~sel1, sel0);  // AND_Gate
  and and_19 (and_19_out, e18, sel4, ~se3, ~sel2, sel1, ~sel0);  // AND_Gate
  and and_20 (and_20_out, e19, sel4, ~se3, ~sel2, sel1, sel0);  // AND_Gate
  and and_21 (and_21_out, e20, sel4, ~se3, sel2, ~sel1, ~sel0);  // AND_Gate
  and and_22 (and_22_out, e21, sel4, ~se3, sel2, ~sel1, sel0);  // AND_Gate
  and and_23 (and_23_out, e22, sel4, ~se3, sel2, sel1, ~sel0);  // AND_Gate
  and and_24 (and_24_out, e23, sel4, ~se3, sel2, sel1, sel0);  // AND_Gate
  and and_25 (and_25_out, e24, sel4, se3, ~sel2, ~sel1, ~sel0);  // AND_Gate
  and and_26 (and_26_out, e25, sel4, se3, ~sel2, ~sel1, sel0);  // AND_Gate
  and and_27 (and_27_out, e26, sel4, se3, ~sel2, sel1, ~sel0);  // AND_Gate
  and and_28 (and_28_out, e27, sel4, se3, ~sel2, sel1, sel0);  // AND_Gate
  and and_29 (and_29_out, e28, sel4, se3, sel2, ~sel1, ~sel0);  // AND_Gate
  and and_30 (and_30_out, e29, sel4, se3, sel2, ~sel1, sel0);  // AND_Gate
  and and_31 (and_31_out, e30, sel4, se3, sel2, sel1, ~sel0);  // AND_Gate
  and and_32 (and_32_out, e31, sel4, se3, sel2, sel1, sel0);
  or or_1 (Saida, and_1_out, and_2_out, and_3_out, and_4_out, and_5_out, and_6_out, and_7_out, and_8_out, and_9_out, and_10_out, and_11_out, and_12_out, and_13_out, and_14_out, and_15_out, and_16_out, and_17_out, and_18_out, and_19_out, and_20_out, and_21_out, and_22_out, and_23_out, and_24_out, and_25_out, and_26_out, and_27_out, and_28_out, and_29_out, and_30_out, and_31_out, and_32_out);
endmodule
