// Logisim project ula.circ as structural Verilog: 14 circuits, main circuit main
module main (
  input  [31:0] A,
  input  [31:0] B,
  input  [4:0] sel,
  output Zero,
  output Overflow,
  output [31:0] S
);

  wire sradetect_1_s, srldetect_1_s, ssldetect_1_s;
  wire [31:0] shiftlogicalleft32_1_out_3, shiftlogicalright32_1_out_3, shiftrightarith_1_out_3;

  SSLDetect ssldetect_1 (.sel(sel), .s(ssldetect_1_s));
  shiftlogicalleft32 shiftlogicalleft32_1 (.in_1(B), .s(ssldetect_1_s), .out_3(shiftlogicalleft32_1_out_3));
  shiftlogicalright32 shiftlogicalright32_1 (
    .in_1(shiftlogicalleft32_1_out_3), .s(srldetect_1_s), .out_3(shiftlogicalright32_1_out_3));
  SRLDetect srldetect_1 (.sel(sel), .s(srldetect_1_s));
  shiftrightarith shiftrightarith_1 (
    .in_1(shiftlogicalright32_1_out_3), .s(sradetect_1_s), .out_3(shiftrightarith_1_out_3));
  SRADetect sradetect_1 (.sel(sel), .s(sradetect_1_s));
  ula_cell ula_cell_1 (.vai(Overflow), .out_5(S), .vem(1'b0), .b(shiftrightarith_1_out_3), .a(A), .sel(sel));
  nor nor_1 (Zero, S[0], S[1], S[2], S[3], S[4], S[5], S[6], S[7], S[8], S[9], S[10], S[11], S[12], S[13], S[14], S[15], S[16], S[17], S[18], S[19], S[20], S[21], S[22], S[23], S[24], S[25], S[26], S[27], S[28], S[29], S[30], S[31]);

  // Notes on the sheet:
  //   4
  //   5
  //   6
  //   0 = and; 1 = or; 2 = soma; 3 = xor; 4 = shiftleft b; 5 = rightshigtlogical b; 6 = shift arith right
endmodule

module mux32 (
  input  e0,
  input  e1,
  input  e2,
  input  e3,
  input  e4,
  input  e5,
  input  e6,
  input  e7,
  input  e8,
  input  e9,
  input  e10,
  input  e11,
  input  e12,
  input  e13,
  input  e14,
  input  e15,
  input  e16,
  input  e17,
  input  e18,
  input  e19,
  input  e20,
  input  e21,
  input  e22,
  input  e23,
  input  e24,
  input  e25,
  input  e26,
  input  e27,
  input  e28,
  input  e29,
  input  e30,
  input  e31,
  input  sel4,
  input  se3,
  input  sel2,
  input  sel1,
  input  sel0,
  output Saida
);

  wire and_1_out, and_2_out, and_3_out, and_4_out, and_5_out, and_6_out, and_7_out, and_8_out, and_9_out,
       and_10_out, and_11_out, and_12_out, and_13_out, and_14_out, and_15_out, and_16_out, and_17_out,
       and_18_out, and_19_out, and_20_out, and_21_out, and_22_out, and_23_out, and_24_out, and_25_out,
       and_26_out, and_27_out, and_28_out, and_29_out, and_30_out, and_31_out, and_32_out;

  and and_1 (and_1_out, e0, ~sel4, ~se3, ~sel2, ~sel1, ~sel0);  // AND_Gate
  and and_2 (and_2_out, e1, ~sel4, ~se3, ~sel2, ~sel1, sel0);  // AND_Gate
  and and_3 (and_3_out, e2, ~sel4, ~se3, ~sel2, sel1, ~sel0);  // AND_Gate
  and and_4 (and_4_out, e3, ~sel4, ~se3, ~sel2, sel1, sel0);  // AND_Gate
  and and_5 (and_5_out, e4, ~sel4, ~se3, sel2, ~sel1, ~sel0);  // AND_Gate
  and and_6 (and_6_out, e5, ~sel4, ~se3, sel2, ~sel1, sel0);  // AND_Gate
  and and_7 (and_7_out, e6, ~sel4, ~se3, sel2, sel1, ~sel0);  // AND_Gate
  and and_8 (and_8_out, e7, ~sel4, ~se3, sel2, sel1, sel0);  // AND_Gate
  and and_9 (and_9_out, e8, ~sel4, se3, ~sel2, ~sel1, ~sel0);  // AND_Gate
  and and_10 (and_10_out, e9, ~sel4, se3, ~sel2, ~sel1, sel0);  // AND_Gate
  and and_11 (and_11_out, e10, ~sel4, se3, ~sel2, sel1, ~sel0);  // AND_Gate
  and and_12 (and_12_out, e11, ~sel4, se3, ~sel2, sel1, sel0);  // AND_Gate
  and and_13 (and_13_out, e12, ~sel4, se3, sel2, ~sel1, ~sel0);  // AND_Gate
  and and_14 (and_14_out, e13, ~sel4, se3, sel2, ~sel1, sel0);  // AND_Gate
  and and_15 (and_15_out, e14, ~sel4, se3, sel2, sel1, ~sel0);  // AND_Gate
  and and_16 (and_16_out, e15, ~sel4, se3, sel2, sel1, sel0);  // AND_Gate
  and and_17 (and_17_out, e16, sel4, ~se3, ~sel2, ~sel1, ~sel0);  // AND_Gate
  and and_18 (and_18_out, e17, sel4, ~se3, ~sel2, ~sel1, sel0);  // AND_Gate
  and and_19 (and_19_out, e18, sel4, ~se3, ~sel2, sel1, ~sel0);  // AND_Gate
  and and_20 (and_20_out, e19, sel4, ~se3, ~sel2, sel1, sel0);  // AND_Gate
  and and_21 (and_21_out, e20, sel4, ~se3, sel2, ~sel1, ~sel0);  // AND_Gate
  and and_22 (and_22_out, e21, sel4, ~se3, sel2, ~sel1, sel0);  // AND_Gate
  and and_23 (and_23_out, e22, sel4, ~se3, sel2, sel1, ~sel0);  // AND_Gate
  and and_24 (and_24_out, e23, sel4, ~se3, sel2, sel1, sel0);  // AND_Gate
  and and_25 (and_25_out, e24, sel4, se3, ~sel2, ~sel1, ~sel0);  // AND_Gate
  and and_26 (and_26_out, e25, sel4, se3, ~sel2, ~sel1, sel0);  // AND_Gate
  and and_27 (and_27_out, e26, sel4, se3, ~sel2, sel1, ~sel0);  // AND_Gate
  and and_28 (and_28_out, e27, sel4, se3, ~sel2, sel1, sel0);  // AND_Gate
  and and_29 (and_29_out, e28, sel4, se3, sel2, ~sel1, ~sel0);  // AND_Gate
  and and_30 (and_30_out, e29, sel4, se3, sel2, ~sel1, sel0);  // AND_Gate
  and and_31 (and_31_out, e30, sel4, se3, sel2, sel1, ~sel0);  // AND_Gate
  and and_32 (and_32_out, e31, sel4, se3, sel2, sel1, sel0);
  or or_1 (Saida, and_1_out, and_2_out, and_3_out, and_4_out, and_5_out, and_6_out, and_7_out, and_8_out, and_9_out, and_10_out, and_11_out, and_12_out, and_13_out, and_14_out, and_15_out, and_16_out, and_17_out, and_18_out, and_19_out, and_20_out, and_21_out, and_22_out, and_23_out, and_24_out, and_25_out, and_26_out, and_27_out, and_28_out, and_29_out, and_30_out, and_31_out, and_32_out);
endmodule

module somador1bit (
  input  vem1,
  input  a,
  input  b,
  output s,
  output vai1
);

  wire and_1_out, and_2_out, and_3_out, and_4_out, and_5_out, and_6_out, and_7_out;

  and and_1 (and_1_out, ~a, ~b, vem1);  // AND_Gate
  and and_2 (and_2_out, ~a, b, ~vem1);  // AND_Gate
  and and_3 (and_3_out, a, ~b, ~vem1);  // AND_Gate
  and and_4 (and_4_out, a, b, vem1);
  and and_5 (and_5_out, a, ~b, vem1);  // AND_Gate
  and and_6 (and_6_out, a, b, ~vem1);  // AND_Gate
  and and_7 (and_7_out, ~a, b, vem1);  // AND_Gate
  or or_1 (s, and_1_out, and_2_out, and_3_out, and_4_out);
  or or_2 (vai1, and_4_out, and_5_out, and_6_out, and_7_out);
endmodule

module somador32 (
  input  vem,
  input  [31:0] a,
  input  [31:0] b,
  output [31:0] soma,
  output vai
);

  wire somador1bit_2_vai1, somador1bit_3_vai1, somador1bit_4_vai1, somador1bit_5_vai1, somador1bit_6_vai1,
       somador1bit_7_vai1, somador1bit_8_vai1, somador1bit_9_vai1, somador1bit_10_vai1, somador1bit_11_vai1,
       somador1bit_12_vai1, somador1bit_13_vai1, somador1bit_14_vai1, somador1bit_15_vai1,
       somador1bit_16_vai1, somador1bit_17_vai1, somador1bit_18_vai1, somador1bit_19_vai1,
       somador1bit_20_vai1, somador1bit_21_vai1, somador1bit_22_vai1, somador1bit_23_vai1,
       somador1bit_24_vai1, somador1bit_25_vai1, somador1bit_26_vai1, somador1bit_27_vai1,
       somador1bit_28_vai1, somador1bit_29_vai1, somador1bit_30_vai1, somador1bit_31_vai1,
       somador1bit_32_vai1;

  somador1bit somador1bit_1 (.a(a[31]), .b(b[31]), .s(soma[31]), .vem1(somador1bit_2_vai1), .vai1(vai));
  somador1bit somador1bit_2 (.a(a[30]), .b(b[30]), .s(soma[30]), .vem1(somador1bit_3_vai1), .vai1(somador1bit_2_vai1));
  somador1bit somador1bit_3 (.a(a[29]), .b(b[29]), .s(soma[29]), .vem1(somador1bit_4_vai1), .vai1(somador1bit_3_vai1));
  somador1bit somador1bit_4 (.a(a[28]), .b(b[28]), .s(soma[28]), .vem1(somador1bit_5_vai1), .vai1(somador1bit_4_vai1));
  somador1bit somador1bit_5 (.a(a[27]), .b(b[27]), .s(soma[27]), .vem1(somador1bit_7_vai1), .vai1(somador1bit_5_vai1));
  somador1bit somador1bit_6 (.a(a[25]), .b(b[25]), .s(soma[25]), .vem1(somador1bit_8_vai1), .vai1(somador1bit_6_vai1));
  somador1bit somador1bit_7 (.a(a[26]), .b(b[26]), .s(soma[26]), .vem1(somador1bit_6_vai1), .vai1(somador1bit_7_vai1));
  somador1bit somador1bit_8 (.a(a[24]), .b(b[24]), .s(soma[24]), .vem1(somador1bit_9_vai1), .vai1(somador1bit_8_vai1));
  somador1bit somador1bit_9 (.a(a[23]), .b(b[23]), .s(soma[23]), .vem1(somador1bit_10_vai1), .vai1(somador1bit_9_vai1));
  somador1bit somador1bit_10 (
    .a(a[22]), .b(b[22]), .s(soma[22]), .vem1(somador1bit_11_vai1), .vai1(somador1bit_10_vai1));
  somador1bit somador1bit_11 (
    .a(a[21]), .b(b[21]), .s(soma[21]), .vem1(somador1bit_12_vai1), .vai1(somador1bit_11_vai1));
  somador1bit somador1bit_12 (
    .a(a[20]), .b(b[20]), .s(soma[20]), .vem1(somador1bit_13_vai1), .vai1(somador1bit_12_vai1));
  somador1bit somador1bit_13 (
    .a(a[19]), .b(b[19]), .s(soma[19]), .vem1(somador1bit_15_vai1), .vai1(somador1bit_13_vai1));
  somador1bit somador1bit_14 (
    .a(a[17]), .b(b[17]), .s(soma[17]), .vem1(somador1bit_16_vai1), .vai1(somador1bit_14_vai1));
  somador1bit somador1bit_15 (
    .a(a[18]), .b(b[18]), .s(soma[18]), .vem1(somador1bit_14_vai1), .vai1(somador1bit_15_vai1));
  somador1bit somador1bit_16 (
    .a(a[16]), .b(b[16]), .s(soma[16]), .vem1(somador1bit_17_vai1), .vai1(somador1bit_16_vai1));
  somador1bit somador1bit_17 (
    .a(a[15]), .b(b[15]), .s(soma[15]), .vem1(somador1bit_18_vai1), .vai1(somador1bit_17_vai1));
  somador1bit somador1bit_18 (
    .a(a[14]), .b(b[14]), .s(soma[14]), .vem1(somador1bit_19_vai1), .vai1(somador1bit_18_vai1));
  somador1bit somador1bit_19 (
    .a(a[13]), .b(b[13]), .s(soma[13]), .vem1(somador1bit_20_vai1), .vai1(somador1bit_19_vai1));
  somador1bit somador1bit_20 (
    .a(a[12]), .b(b[12]), .s(soma[12]), .vem1(somador1bit_21_vai1), .vai1(somador1bit_20_vai1));
  somador1bit somador1bit_21 (
    .a(a[11]), .b(b[11]), .s(soma[11]), .vem1(somador1bit_23_vai1), .vai1(somador1bit_21_vai1));
  somador1bit somador1bit_22 (.a(a[9]), .b(b[9]), .s(soma[9]), .vem1(somador1bit_24_vai1), .vai1(somador1bit_22_vai1));
  somador1bit somador1bit_23 (
    .a(a[10]), .b(b[10]), .s(soma[10]), .vem1(somador1bit_22_vai1), .vai1(somador1bit_23_vai1));
  somador1bit somador1bit_24 (.a(a[8]), .b(b[8]), .s(soma[8]), .vem1(somador1bit_25_vai1), .vai1(somador1bit_24_vai1));
  somador1bit somador1bit_25 (.a(a[7]), .b(b[7]), .s(soma[7]), .vem1(somador1bit_26_vai1), .vai1(somador1bit_25_vai1));
  somador1bit somador1bit_26 (.a(a[6]), .b(b[6]), .s(soma[6]), .vem1(somador1bit_27_vai1), .vai1(somador1bit_26_vai1));
  somador1bit somador1bit_27 (.a(a[5]), .b(b[5]), .s(soma[5]), .vem1(somador1bit_28_vai1), .vai1(somador1bit_27_vai1));
  somador1bit somador1bit_28 (.a(a[4]), .b(b[4]), .s(soma[4]), .vem1(somador1bit_29_vai1), .vai1(somador1bit_28_vai1));
  somador1bit somador1bit_29 (.a(a[3]), .b(b[3]), .s(soma[3]), .vem1(somador1bit_30_vai1), .vai1(somador1bit_29_vai1));
  somador1bit somador1bit_30 (.a(a[2]), .b(b[2]), .s(soma[2]), .vem1(somador1bit_31_vai1), .vai1(somador1bit_30_vai1));
  somador1bit somador1bit_31 (.a(a[1]), .b(b[1]), .s(soma[1]), .vem1(somador1bit_32_vai1), .vai1(somador1bit_31_vai1));
  somador1bit somador1bit_32 (.a(a[0]), .b(b[0]), .s(soma[0]), .vem1(vem), .vai1(somador1bit_32_vai1));
endmodule

module shiftlogicalleft32 (
  input  [31:0] in_1,
  input  s,
  output [31:0] out_3
);

  mux2_32bit mux2_32bit_1 (.a(in_1), .in_2({in_1[30:0], 1'b0}), .sel(s), .s(out_3));
endmodule

module mux2_32bit (
  input  [31:0] a,
  input  [31:0] in_2,
  input  sel,
  output [31:0] s
);

  wire [31:0] and_1_out, and_2_out;

  assign and_1_out = a & ~{32{sel}};  // AND_Gate and_1, 32 bits wide
  assign and_2_out = in_2 & {32{sel}};  // AND_Gate and_2, 32 bits wide
  assign s = and_1_out | and_2_out;  // OR_Gate or_1, 32 bits wide
endmodule

module shiftlogicalright32 (
  input  [31:0] in_1,
  input  s,
  output [31:0] out_3
);

  mux2_32bit mux2_32bit_1 (.a(in_1), .in_2({1'b0, in_1[31:1]}), .sel(s), .s(out_3));
endmodule

module ula_cell (
  input  [31:0] b,
  input  [31:0] a,
  input  vem,
  input  [4:0] sel,
  output [31:0] out_5,
  output vai
);

  wire [31:0] and_1_out, nand_1_out, or_1_out, somador32_1_soma, undriven, undriven_2, undriven_3,
       undriven_4, undriven_5, undriven_6, undriven_7, undriven_8, undriven_9, undriven_10, undriven_11,
       undriven_12, undriven_13, undriven_14, undriven_15, undriven_16, undriven_17, undriven_18,
       undriven_19, undriven_20, undriven_21, undriven_22, undriven_23, undriven_24, xor_1_out;

  somador32 somador32_1 (.a(a), .b(b), .soma(somador32_1_soma), .vai(vai), .vem(vem));
  assign xor_1_out = a ^ b;  // XOR_Gate xor_1, 32 bits wide
  assign nand_1_out = ~(~a & b);  // NAND_Gate nand_1, 32 bits wide
  assign and_1_out = a & b;  // AND_Gate and_1, 32 bits wide
  assign or_1_out = a | b;  // OR_Gate or_1, 32 bits wide
  mux32_32bits32entrada mux32_32bits32entrada_1 (
    .e0(and_1_out), .e1(or_1_out), .e2(somador32_1_soma), .e3(xor_1_out), .e4(b), .e5(b), .e6(b),
    .e7(undriven), .e8(undriven_2), .e9(undriven_3), .e10(undriven_4), .e11(undriven_5), .e12(undriven_6),
    .e13(undriven_7), .e14(undriven_8), .e15(undriven_9), .e16(undriven_10), .e17(undriven_11),
    .e18(undriven_12), .e19(undriven_13), .e20(undriven_14), .e21(undriven_15), .e22(undriven_16),
    .e23(undriven_17), .e24(undriven_18), .e25(undriven_19), .e26(undriven_20), .e27(undriven_21),
    .e28(undriven_22), .e29(undriven_23), .e30(undriven_24), .e31(nand_1_out), .sel4(sel[4]), .se3(sel[3]),
    .sel2(sel[2]), .sel1(sel[1]), .sel0(sel[0]), .Saida(out_5));
endmodule

module mux32_1entrada (
  input  [31:0] e,
  input  [4:0] sel,
  output Saida
);

  wire and_1_out, and_2_out, and_3_out, and_4_out, and_5_out, and_6_out, and_7_out, and_8_out, and_9_out,
       and_10_out, and_11_out, and_12_out, and_13_out, and_14_out, and_15_out, and_16_out, and_17_out,
       and_18_out, and_19_out, and_20_out, and_21_out, and_22_out, and_23_out, and_24_out, and_25_out,
       and_26_out, and_27_out, and_28_out, and_29_out, and_30_out, and_31_out, and_32_out;

  and and_1 (and_1_out, e[0], ~sel[4], ~sel[3], ~sel[2], ~sel[1], ~sel[0]);  // AND_Gate
  and and_2 (and_2_out, e[1], ~sel[4], ~sel[3], ~sel[2], ~sel[1], sel[0]);  // AND_Gate
  and and_3 (and_3_out, e[2], ~sel[4], ~sel[3], ~sel[2], sel[1], ~sel[0]);  // AND_Gate
  and and_4 (and_4_out, e[3], ~sel[4], ~sel[3], ~sel[2], sel[1], sel[0]);  // AND_Gate
  and and_5 (and_5_out, e[4], ~sel[4], ~sel[3], sel[2], ~sel[1], ~sel[0]);  // AND_Gate
  and and_6 (and_6_out, e[5], ~sel[4], ~sel[3], sel[2], ~sel[1], sel[0]);  // AND_Gate
  and and_7 (and_7_out, e[6], ~sel[4], ~sel[3], sel[2], sel[1], ~sel[0]);  // AND_Gate
  and and_8 (and_8_out, e[7], ~sel[4], ~sel[3], sel[2], sel[1], sel[0]);  // AND_Gate
  and and_9 (and_9_out, e[8], ~sel[4], sel[3], ~sel[2], ~sel[1], ~sel[0]);  // AND_Gate
  and and_10 (and_10_out, e[9], ~sel[4], sel[3], ~sel[2], ~sel[1], sel[0]);  // AND_Gate
  and and_11 (and_11_out, e[10], ~sel[4], sel[3], ~sel[2], sel[1], ~sel[0]);  // AND_Gate
  and and_12 (and_12_out, e[11], ~sel[4], sel[3], ~sel[2], sel[1], sel[0]);  // AND_Gate
  and and_13 (and_13_out, e[12], ~sel[4], sel[3], sel[2], ~sel[1], ~sel[0]);  // AND_Gate
  and and_14 (and_14_out, e[13], ~sel[4], sel[3], sel[2], ~sel[1], sel[0]);  // AND_Gate
  and and_15 (and_15_out, e[14], ~sel[4], sel[3], sel[2], sel[1], ~sel[0]);  // AND_Gate
  and and_16 (and_16_out, e[15], ~sel[4], sel[3], sel[2], sel[1], sel[0]);  // AND_Gate
  and and_17 (and_17_out, e[16], sel[4], ~sel[3], ~sel[2], ~sel[1], ~sel[0]);  // AND_Gate
  and and_18 (and_18_out, e[17], sel[4], ~sel[3], ~sel[2], ~sel[1], sel[0]);  // AND_Gate
  and and_19 (and_19_out, e[18], sel[4], ~sel[3], ~sel[2], sel[1], ~sel[0]);  // AND_Gate
  and and_20 (and_20_out, e[19], sel[4], ~sel[3], ~sel[2], sel[1], sel[0]);  // AND_Gate
  and and_21 (and_21_out, e[20], sel[4], ~sel[3], sel[2], ~sel[1], ~sel[0]);  // AND_Gate
  and and_22 (and_22_out, e[21], sel[4], ~sel[3], sel[2], ~sel[1], sel[0]);  // AND_Gate
  and and_23 (and_23_out, e[22], sel[4], ~sel[3], sel[2], sel[1], ~sel[0]);  // AND_Gate
  and and_24 (and_24_out, e[23], sel[4], ~sel[3], sel[2], sel[1], sel[0]);  // AND_Gate
  and and_25 (and_25_out, e[24], sel[4], sel[3], ~sel[2], ~sel[1], ~sel[0]);  // AND_Gate
  and and_26 (and_26_out, e[25], sel[4], sel[3], ~sel[2], ~sel[1], sel[0]);  // AND_Gate
  and and_27 (and_27_out, e[26], sel[4], sel[3], ~sel[2], sel[1], ~sel[0]);  // AND_Gate
  and and_28 (and_28_out, e[27], sel[4], sel[3], ~sel[2], sel[1], sel[0]);  // AND_Gate
  and and_29 (and_29_out, e[28], sel[4], sel[3], sel[2], ~sel[1], ~sel[0]);  // AND_Gate
  and and_30 (and_30_out, e[29], sel[4], sel[3], sel[2], ~sel[1], sel[0]);  // AND_Gate
  and and_31 (and_31_out, e[30], sel[4], sel[3], sel[2], sel[1], ~sel[0]);  // AND_Gate
  and and_32 (and_32_out, e[31], sel[4], sel[3], sel[2], sel[1], sel[0]);
  or or_1 (Saida, and_1_out, and_2_out, and_3_out, and_4_out, and_5_out, and_6_out, and_7_out, and_8_out, and_9_out, and_10_out, and_11_out, and_12_out, and_13_out, and_14_out, and_15_out, and_16_out, and_17_out, and_18_out, and_19_out, and_20_out, and_21_out, and_22_out, and_23_out, and_24_out, and_25_out, and_26_out, and_27_out, and_28_out, and_29_out, and_30_out, and_31_out, and_32_out);
endmodule

module mux32_32bits32entrada (
  input  [31:0] e0,
  input  [31:0] e1,
  input  [31:0] e2,
  input  [31:0] e3,
  input  [31:0] e4,
  input  [31:0] e5,
  input  [31:0] e6,
  input  [31:0] e7,
  input  [31:0] e8,
  input  [31:0] e9,
  input  [31:0] e10,
  input  [31:0] e11,
  input  [31:0] e12,
  input  [31:0] e13,
  input  [31:0] e14,
  input  [31:0] e15,
  input  [31:0] e16,
  input  [31:0] e17,
  input  [31:0] e18,
  input  [31:0] e19,
  input  [31:0] e20,
  input  [31:0] e21,
  input  [31:0] e22,
  input  [31:0] e23,
  input  [31:0] e24,
  input  [31:0] e25,
  input  [31:0] e26,
  input  [31:0] e27,
  input  [31:0] e28,
  input  [31:0] e29,
  input  [31:0] e30,
  input  [31:0] e31,
  input  sel4,
  input  se3,
  input  sel2,
  input  sel1,
  input  sel0,
  output [31:0] Saida
);

  wire [31:0] and_1_out, and_2_out, and_3_out, and_4_out, and_5_out, and_6_out, and_7_out, and_8_out,
       and_9_out, and_10_out, and_11_out, and_12_out, and_13_out, and_14_out, and_15_out, and_16_out,
       and_17_out, and_18_out, and_19_out, and_20_out, and_21_out, and_22_out, and_23_out, and_24_out,
       and_25_out, and_26_out, and_27_out, and_28_out, and_29_out, and_30_out, and_31_out, and_32_out;

  assign and_1_out = e0 & ~{32{sel4}} & ~{32{se3}} & ~{32{sel2}} & ~{32{sel1}} & ~{32{sel0}};  // AND_Gate and_1, 32 bits wide
  assign and_2_out = e1 & ~{32{sel4}} & ~{32{se3}} & ~{32{sel2}} & ~{32{sel1}} & {32{sel0}};  // AND_Gate and_2, 32 bits wide
  assign and_3_out = e2 & ~{32{sel4}} & ~{32{se3}} & ~{32{sel2}} & {32{sel1}} & ~{32{sel0}};  // AND_Gate and_3, 32 bits wide
  assign and_4_out = e3 & ~{32{sel4}} & ~{32{se3}} & ~{32{sel2}} & {32{sel1}} & {32{sel0}};  // AND_Gate and_4, 32 bits wide
  assign and_5_out = e4 & ~{32{sel4}} & ~{32{se3}} & {32{sel2}} & ~{32{sel1}} & ~{32{sel0}};  // AND_Gate and_5, 32 bits wide
  assign and_6_out = e5 & ~{32{sel4}} & ~{32{se3}} & {32{sel2}} & ~{32{sel1}} & {32{sel0}};  // AND_Gate and_6, 32 bits wide
  assign and_7_out = e6 & ~{32{sel4}} & ~{32{se3}} & {32{sel2}} & {32{sel1}} & ~{32{sel0}};  // AND_Gate and_7, 32 bits wide
  assign and_8_out = e7 & ~{32{sel4}} & ~{32{se3}} & {32{sel2}} & {32{sel1}} & {32{sel0}};  // AND_Gate and_8, 32 bits wide
  assign and_9_out = e8 & ~{32{sel4}} & {32{se3}} & ~{32{sel2}} & ~{32{sel1}} & ~{32{sel0}};  // AND_Gate and_9, 32 bits wide
  assign and_10_out = e9 & ~{32{sel4}} & {32{se3}} & ~{32{sel2}} & ~{32{sel1}} & {32{sel0}};  // AND_Gate and_10, 32 bits wide
  assign and_11_out = e10 & ~{32{sel4}} & {32{se3}} & ~{32{sel2}} & {32{sel1}} & ~{32{sel0}};  // AND_Gate and_11, 32 bits wide
  assign and_12_out = e11 & ~{32{sel4}} & {32{se3}} & ~{32{sel2}} & {32{sel1}} & {32{sel0}};  // AND_Gate and_12, 32 bits wide
  assign and_13_out = e12 & ~{32{sel4}} & {32{se3}} & {32{sel2}} & ~{32{sel1}} & ~{32{sel0}};  // AND_Gate and_13, 32 bits wide
  assign and_14_out = e13 & ~{32{sel4}} & {32{se3}} & {32{sel2}} & ~{32{sel1}} & {32{sel0}};  // AND_Gate and_14, 32 bits wide
  assign and_15_out = e14 & ~{32{sel4}} & {32{se3}} & {32{sel2}} & {32{sel1}} & ~{32{sel0}};  // AND_Gate and_15, 32 bits wide
  assign and_16_out = e15 & ~{32{sel4}} & {32{se3}} & {32{sel2}} & {32{sel1}} & {32{sel0}};  // AND_Gate and_16, 32 bits wide
  assign and_17_out = e16 & {32{sel4}} & ~{32{se3}} & ~{32{sel2}} & ~{32{sel1}} & ~{32{sel0}};  // AND_Gate and_17, 32 bits wide
  assign and_18_out = e17 & {32{sel4}} & ~{32{se3}} & ~{32{sel2}} & ~{32{sel1}} & {32{sel0}};  // AND_Gate and_18, 32 bits wide
  assign and_19_out = e18 & {32{sel4}} & ~{32{se3}} & ~{32{sel2}} & {32{sel1}} & ~{32{sel0}};  // AND_Gate and_19, 32 bits wide
  assign and_20_out = e19 & {32{sel4}} & ~{32{se3}} & ~{32{sel2}} & {32{sel1}} & {32{sel0}};  // AND_Gate and_20, 32 bits wide
  assign and_21_out = e20 & {32{sel4}} & ~{32{se3}} & {32{sel2}} & ~{32{sel1}} & ~{32{sel0}};  // AND_Gate and_21, 32 bits wide
  assign and_22_out = e21 & {32{sel4}} & ~{32{se3}} & {32{sel2}} & ~{32{sel1}} & {32{sel0}};  // AND_Gate and_22, 32 bits wide
  assign and_23_out = e22 & {32{sel4}} & ~{32{se3}} & {32{sel2}} & {32{sel1}} & ~{32{sel0}};  // AND_Gate and_23, 32 bits wide
  assign and_24_out = e23 & {32{sel4}} & ~{32{se3}} & {32{sel2}} & {32{sel1}} & {32{sel0}};  // AND_Gate and_24, 32 bits wide
  assign and_25_out = e24 & {32{sel4}} & {32{se3}} & ~{32{sel2}} & ~{32{sel1}} & ~{32{sel0}};  // AND_Gate and_25, 32 bits wide
  assign and_26_out = e25 & {32{sel4}} & {32{se3}} & ~{32{sel2}} & ~{32{sel1}} & {32{sel0}};  // AND_Gate and_26, 32 bits wide
  assign and_27_out = e26 & {32{sel4}} & {32{se3}} & ~{32{sel2}} & {32{sel1}} & ~{32{sel0}};  // AND_Gate and_27, 32 bits wide
  assign and_28_out = e27 & {32{sel4}} & {32{se3}} & ~{32{sel2}} & {32{sel1}} & {32{sel0}};  // AND_Gate and_28, 32 bits wide
  assign and_29_out = e28 & {32{sel4}} & {32{se3}} & {32{sel2}} & ~{32{sel1}} & ~{32{sel0}};  // AND_Gate and_29, 32 bits wide
  assign and_30_out = e29 & {32{sel4}} & {32{se3}} & {32{sel2}} & ~{32{sel1}} & {32{sel0}};  // AND_Gate and_30, 32 bits wide
  assign and_31_out = e30 & {32{sel4}} & {32{se3}} & {32{sel2}} & {32{sel1}} & ~{32{sel0}};  // AND_Gate and_31, 32 bits wide
  assign and_32_out = e31 & {32{sel4}} & {32{se3}} & {32{sel2}} & {32{sel1}} & {32{sel0}};  // AND_Gate and_32, 32 bits wide
  assign Saida = and_1_out | and_2_out | and_3_out | and_4_out | and_5_out | and_6_out | and_7_out | and_8_out | and_9_out | and_10_out | and_11_out | and_12_out | and_13_out | and_14_out | and_15_out | and_16_out | and_17_out | and_18_out | and_19_out | and_20_out | and_21_out | and_22_out | and_23_out | and_24_out | and_25_out | and_26_out | and_27_out | and_28_out | and_29_out | and_30_out | and_31_out | and_32_out;  // OR_Gate or_1, 32 bits wide
endmodule

module shiftrightarith (
  input  [31:0] in_1,
  input  s,
  output [31:0] out_3
);

  mux2_32bit mux2_32bit_1 (.a(in_1), .in_2({{2{in_1[31]}}, in_1[30:1]}), .sel(s), .s(out_3));
endmodule

module SSLDetect (
  input  [4:0] sel,
  output s
);

  and and_1 (s, ~sel[0], ~sel[1], sel[2], ~sel[3], ~sel[4]);  // AND_Gate

  // Notes on the sheet:
  //   4
endmodule

module SRLDetect (
  input  [4:0] sel,
  output s
);

  and and_1 (s, sel[0], ~sel[1], sel[2], ~sel[3], ~sel[4]);  // AND_Gate

  // Notes on the sheet:
  //   5
endmodule

module SRADetect (
  input  [4:0] sel,
  output s
);

  and and_1 (s, ~sel[0], sel[1], sel[2], ~sel[3], ~sel[4]);  // AND_Gate

  // Notes on the sheet:
  //   6
endmodule
