// Logisim project IntroducaoMux.circ as structural Verilog
module MUXd2 (
  input  A,
  input  B,
  input  Sel,
  output S
);

  wire and_1_out, and_2_out;

  and and_1 (and_1_out, A, ~Sel);  // AND_Gate
  and and_2 (and_2_out, B, Sel);
  or or_1 (S, and_1_out, and_2_out);
endmodule

module MUXd4 (
  input  A,
  input  B,
  input  C,
  input  D,
  input  Sel1,
  input  Sel2,
  output S
);

  wire muxd2_1_s, muxd2_2_s;

  MUXd2 muxd2_1 (.A(A), .B(B), .Sel(Sel2), .S(muxd2_1_s));
  MUXd2 muxd2_2 (.A(C), .B(D), .Sel(Sel2), .S(muxd2_2_s));
  MUXd2 muxd2_3 (.A(muxd2_1_s), .B(muxd2_2_s), .Sel(Sel1), .S(S));
endmodule

module MUXd4B (
  input  A,
  input  B,
  input  C,
  input  D,
  input  [1:0] Sel,
  output out_6
);

  wire and_1_out, and_2_out, and_3_out, and_4_out;

  and and_1 (and_1_out, A, ~Sel[0], ~Sel[1]);  // AND_Gate
  and and_2 (and_2_out, B, ~Sel[0], Sel[1]);  // AND_Gate
  and and_3 (and_3_out, C, Sel[0], ~Sel[1]);  // AND_Gate
  and and_4 (and_4_out, D, Sel[0], Sel[1]);
  or or_1 (out_6, and_1_out, and_2_out, and_3_out, and_4_out);
endmodule
